# Fritzing sketch TRANSMITTER (saved by Fritzing 1.0.0rc)

parts:
  VCC1 = Battery block 9V
  M1 = RioRand LM2596
  U1 = ESP32-38PinWide [part_number=ESP32-38PinWide]
  S2 = Toggle Switch [package=THT]
  Mod1 = KY-023 Dual Axis Joystick Module [package="Breakout board"]

nets:
  N1: VCC1.-, M1.Pin_2
  N2: VCC1.+, S2.L1
  N3: M1.Pin_1, S2.COM
  N4: M1.Pin_3, U1.3.3, Mod1.+5V
  GND: M1.Pin_4, U1.GND, Mod1.GND
  N5: U1.GPIO32, Mod1.VRx
  N6: U1.GPIO33, Mod1.VRy
  N7: U1.GPIO21, Mod1.SW

notes:
  Set buck to 3.3 V

custom parts:
  ESP32-38PinWide: Generic 38-Pin ESP32 with wide format (only access to one side of pins on a breadboard) based on Stephen Lilley's HiLetgo ESP-WROOM-32 ESP32 ESP-32S Development Board.
  KY-023 Dual Axis Joystick Module: KY-023 Dual-Axis Joystick Module.
